// Logisim project 74179.circ as structural Verilog: 1 circuit, main circuit main
module main (
  input  S1,
  input  S0,
  input  CLR,
  input  IR,
  input  IL,
  input  A,
  input  B,
  input  C,
  input  D,
  output QA,
  output QB,
  output QC,
  output QD
);

  wire n74194_1_pin11;

  _74194 u_74194_1 (
    .pin1(CLR), .pin2(IR), .pin3(A), .pin4(B), .pin5(C), .pin6(D), .pin7(IL), .pin15(QA), .pin14(QB),
    .pin13(QC), .pin12(QD), .pin11(n74194_1_pin11), .pin10(S1), .pin9(S0));
  Clock CLK (.out(n74194_1_pin11));
endmodule
