// Logisim project 8bit_register_2_74719.circ as structural Verilog: 1 circuit, main circuit main
module main (
  input  S1,
  input  S0,
  input  CLR,
  input  IR,
  input  M,
  output QA1,
  output QB1,
  output QC1,
  output QD1,
  output QA2,
  output QB2,
  output QC2,
  output QD2
);

  wire and_1_out, and_2_out, n74194_1_pin11, n74194_2_pin2, not_1_out;

  _74194 u_74194_1 (
    .pin1(CLR), .pin2(IR), .pin15(QA1), .pin14(QB1), .pin13(QC1), .pin12(QD1), .pin11(n74194_1_pin11),
    .pin10(S1), .pin9(S0));  // open: pin3, pin4, pin5, pin6, pin7
  _74194 u_74194_2 (
    .pin1(CLR), .pin2(n74194_2_pin2), .pin15(QA2), .pin14(QB2), .pin13(QC2), .pin12(QD2),
    .pin11(n74194_1_pin11), .pin9(S0));  // open: pin3, pin4, pin5, pin6, pin7, pin10
  or or_1 (n74194_2_pin2, and_1_out, and_2_out);
  buf and_1 (and_1_out, QD1);  // AND_Gate
  // AND_Gate and_2 has open pins: out=and_2_out
  not not_1 (not_1_out, M);
  Clock CLK (.out(n74194_1_pin11));
endmodule
