// Logisim project asygx_dyad_metr_4bit.circ as structural Verilog: 1 circuit, main circuit main
module main (
  input  SET,
  input  CLR,
  output Qa,
  output Qb,
  output Qc,
  output Qd
);

  wire button_1_out;

  Button button_1 (.out(button_1_out));
  J_K_Flip_Flop #(.trigger("falling")) j_k_ff_1 (
    .J(SET), .K(SET), .clk(button_1_out), .Q(Qa), .preset(SET), .reset(CLR));  // open: Qn
  J_K_Flip_Flop #(.trigger("falling")) j_k_ff_2 (
    .J(SET), .K(SET), .clk(Qa), .Q(Qb), .preset(SET), .reset(CLR));  // open: Qn
  J_K_Flip_Flop #(.trigger("falling")) j_k_ff_3 (
    .J(SET), .K(SET), .clk(Qb), .Q(Qc), .preset(SET), .reset(CLR));  // open: Qn
  J_K_Flip_Flop #(.trigger("falling")) j_k_ff_4 (
    .J(SET), .K(SET), .clk(Qc), .Q(Qd), .preset(SET), .reset(CLR));  // open: Qn
endmodule
