// Logisim project erg4.circ as structural Verilog: 2 circuits, main circuit main
module main (
  input  PDIP0,
  input  PDIP1,
  input  PDIP2,
  input  PDIP3,
  input  IR,
  input  CLR,
  output LED3,
  output LED2,
  output LED1,
  output LED0
);

  wire CLK_out, dualjkff_1_q1out, dualjkff_1_q2out, dualjkff_2_q1out, dualjkff_2_q2out, n7404_1_p4;

  Clock CLK (.out(CLK_out));
  // _7404 7404_1: pin names not known; wires that end beside it: 1'b0, 1'b1, IR, n7404_1_p4
  DualJKFF dualjkff_1 (
    .Vcc(1'b1), .PRE1(PDIP3), .J1(IR), .K1(n7404_1_p4), .CLK1(CLK_out), .CLR1(CLR), .PRE2(PDIP2), .J2(LED3),
    .K2(dualjkff_1_q1out), .CLK2(CLK_out), .CLR2(CLR), .GND(1'b0), .Q1(LED3), .Q1out(dualjkff_1_q1out),
    .Q2(LED2), .Q2out(dualjkff_1_q2out));
  DualJKFF dualjkff_2 (
    .Vcc(1'b1), .PRE1(PDIP1), .J1(LED2), .K1(dualjkff_1_q2out), .CLK1(CLK_out), .CLR1(CLR), .PRE2(PDIP0),
    .J2(LED1), .K2(dualjkff_2_q1out), .CLK2(CLK_out), .CLR2(CLR), .GND(1'b0), .Q1(LED1),
    .Q1out(dualjkff_2_q1out), .Q2(LED0), .Q2out(dualjkff_2_q2out));
endmodule

module DualJKFF (
  input  Vcc,
  input  PRE1,
  input  J1,
  input  K1,
  input  CLK1,
  input  CLR1,
  input  PRE2,
  input  J2,
  input  K2,
  input  CLK2,
  input  CLR2,
  input  GND,
  output Q1,
  output Q1out,
  output Q2,
  output Q2out
);

  J_K_Flip_Flop #(.trigger("falling")) j_k_ff_1 (
    .J(J1), .K(K1), .clk(CLK1), .Q(Q1), .Qn(Q1out), .preset(PRE1), .reset(CLR1));
  J_K_Flip_Flop #(.trigger("falling")) j_k_ff_2 (
    .J(J2), .K(K2), .clk(CLK2), .Q(Q2), .Qn(Q2out), .preset(PRE2), .reset(CLR2));
endmodule
