// Logisim project syghronosBCD.circ as structural Verilog: 2 circuits, main circuit main
module main (
  output QD,
  output QC,
  output QB,
  output QA,
  output C
);

  wire button_1_out, doublejkff_1_q1out, doublejkff_1_q2out, doublejkff_2_q1out, n7408_1_pin1, n7408_1_pin5,
       n7408_1_pin6, n7408_1_pin11, n7408_1_pin12;

  Button button_1 (.out(button_1_out));
  _7408 u_7408_1 (
    .pin1(n7408_1_pin1), .pin2(QA), .pin3(C), .pin4(QA), .pin5(n7408_1_pin5), .pin6(n7408_1_pin6),
    .pin13(n7408_1_pin1), .pin12(n7408_1_pin12), .pin11(n7408_1_pin11), .pin10(n7408_1_pin1), .pin9(QC),
    .pin8(n7408_1_pin5));
  DoubleJKFF doublejkff_1 (
    .Vcc(1'b1), .PRE1(1'b1), .K1(1'b1), .CLK1(button_1_out), .CLR1(1'b1), .PRE2(1'b1), .J2(n7408_1_pin11),
    .K2(n7408_1_pin1), .CLK2(button_1_out), .CLR2(1'b1), .GND(1'b0), .Q1(QD), .Q1out(doublejkff_1_q1out),
    .Q2(QC), .Q2out(doublejkff_1_q2out));  // open: J1
  DoubleJKFF doublejkff_2 (
    .Vcc(1'b1), .PRE1(1'b1), .J1(n7408_1_pin5), .K1(n7408_1_pin5), .CLK1(button_1_out), .CLR1(1'b1),
    .PRE2(1'b1), .J2(n7408_1_pin6), .K2(n7408_1_pin1), .CLK2(button_1_out), .CLR2(1'b1), .GND(1'b0), .Q1(QB),
    .Q1out(doublejkff_2_q1out), .Q2(QA), .Q2out(n7408_1_pin12));
endmodule

module DoubleJKFF (
  input  Vcc,
  input  PRE1,
  input  J1,
  input  K1,
  input  CLK1,
  input  CLR1,
  input  PRE2,
  input  J2,
  input  K2,
  input  CLK2,
  input  CLR2,
  input  GND,
  output Q1,
  output Q1out,
  output Q2,
  output Q2out
);

  J_K_Flip_Flop #(.trigger("falling")) j_k_ff_1 (
    .J(J1), .K(K1), .clk(CLK1), .Q(Q1), .Qn(Q1out), .preset(PRE1), .reset(CLR1));
  J_K_Flip_Flop #(.trigger("falling")) j_k_ff_2 (
    .J(J2), .K(K2), .clk(CLK2), .Q(Q2), .Qn(Q2out), .preset(PRE2), .reset(CLR2));
endmodule
