// Logisim project ylop74193.circ as structural Verilog: 1 circuit, main circuit main
module main (
  input  D,
  input  C,
  input  B,
  input  A,
  input  Load,
  input  Clear,
  input  in_7,
  output QD,
  output QC,
  output QB,
  output QA,
  output Carry,
  output Borrow
);

  wire n74193_1_pin5, n74193_1_pin12, n74193_1_pin14;

  _74193 u_74193_1 (
    .pin1(B), .pin2(QB), .pin3(QA), .pin4(in_7), .pin5(n74193_1_pin5), .pin6(QC), .pin7(QD), .pin15(A),
    .pin14(n74193_1_pin14), .pin13(Borrow), .pin12(n74193_1_pin12), .pin11(n74193_1_pin12), .pin10(C),
    .pin9(D));
  Clock clock_1 (.out(n74193_1_pin5));
  // AND_Gate and_1 has open pins: out=n74193_1_pin14
endmodule
